// Digital circuit 8-bit Memory.dig as structural Verilog
module _8_bit_Memory (
  input  [2:0] Address_Pin,
  input  clk,
  input  [7:0] Data_Input,
  input  [1:0] CTRL,
  output [7:0] Data_Output
);

  wire and_1_out, and_2_out, and_3_out, and_4_out, and_5_out, and_6_out, and_7_out, and_8_out,
       decoder_1_out_0, decoder_1_out_1, decoder_1_out_2, decoder_1_out_3, decoder_1_out_4, decoder_1_out_5,
       decoder_1_out_6, decoder_1_out_7;
  wire [7:0] _8_bit_1_p4, _8_bit_2_p4, _8_bit_3_p4, _8_bit_4_p4, _8_bit_5_p4, _8_bit_6_p4, _8_bit_7_p4,
       _8_bit_8_p4;

  Decoder #(.Selector_Bits(3)) decoder_1 (
    .sel(Address_Pin), .out_0(decoder_1_out_0), .out_1(decoder_1_out_1), .out_2(decoder_1_out_2),
    .out_3(decoder_1_out_3), .out_4(decoder_1_out_4), .out_5(decoder_1_out_5), .out_6(decoder_1_out_6),
    .out_7(decoder_1_out_7));
  and and_1 (and_1_out, clk, decoder_1_out_0);
  and and_2 (and_2_out, clk, decoder_1_out_1);
  and and_3 (and_3_out, clk, decoder_1_out_2);
  and and_4 (and_4_out, clk, decoder_1_out_3);
  and and_5 (and_5_out, clk, decoder_1_out_4);
  and and_6 (and_6_out, clk, decoder_1_out_5);
  and and_7 (and_7_out, clk, decoder_1_out_6);
  and and_8 (and_8_out, clk, decoder_1_out_7);
  // _8_Bit _8_bit_1: pin names not known; wires that end beside it: and_1_out, CTRL, Data_Input, _8_bit_1_p4
  // _8_Bit _8_bit_2: pin names not known; wires that end beside it: and_2_out, CTRL, Data_Input, _8_bit_2_p4
  // _8_Bit _8_bit_3: pin names not known; wires that end beside it: and_3_out, CTRL, Data_Input, _8_bit_3_p4
  // _8_Bit _8_bit_4: pin names not known; wires that end beside it: and_4_out, CTRL, Data_Input, _8_bit_4_p4
  // _8_Bit _8_bit_5: pin names not known; wires that end beside it: and_5_out, CTRL, Data_Input, _8_bit_5_p4
  // _8_Bit _8_bit_6: pin names not known; wires that end beside it: and_6_out, CTRL, Data_Input, _8_bit_6_p4
  // _8_Bit _8_bit_7: pin names not known; wires that end beside it: and_7_out, CTRL, Data_Input, _8_bit_7_p4
  // _8_Bit _8_bit_8: pin names not known; wires that end beside it: and_8_out, CTRL, Data_Input, _8_bit_8_p4
  Multiplexer #(.Selector_Bits(3), .Bits(8)) multiplexer_1 (
    .sel(Address_Pin), .in_0(_8_bit_1_p4), .in_1(_8_bit_2_p4), .in_2(_8_bit_3_p4), .in_3(_8_bit_4_p4),
    .in_4(_8_bit_5_p4), .in_5(_8_bit_6_p4), .in_6(_8_bit_7_p4), .in_7(_8_bit_8_p4), .out(Data_Output));
endmodule
