// Digital circuit 8BitALU.dig as structural Verilog
module _8BitALU (
  input  [7:0] A,
  input  [2:0] S_1_S_0_Carry_In,
  input  [7:0] B,
  output [7:0] Result,
  output Status
);

  wire [7:0] multiplexer_1_out, not_1_out, not_2_out;

  assign not_1_out = ~B;  // Not not_1, 8 bits wide
  assign not_2_out = ~{8{1'b0}};  // Not not_2, 8 bits wide
  Multiplexer #(.Bits(8), .Selector_Bits(2)) multiplexer_1 (
    .sel(S_1_S_0_Carry_In[2:1]), .in_0(B), .in_1(not_1_out), .in_2({8{1'b0}}), .in_3(not_2_out),
    .out(multiplexer_1_out));
  // _8_Bit_Full_Adder _8_bit_full_adder_1: pin names not known; wires that end beside it: A, multiplexer_1_out, S_1_S_0_Carry_In[0], Result, Status
endmodule
