// Digital circuit Control Unit.dig as structural Verilog
module Control_Unit (
  input  clk,
  output Instr_Fetch,
  output Instr_Decode,
  output Instr_Exec,
  output Write_Back
);

  D_FF d_ff_1 (.D(Instr_Exec), .C(clk), .Q(Write_Back));  // open: nQ
  D_FF d_ff_2 (.D(Instr_Decode), .C(clk), .Q(Instr_Exec));  // open: nQ
  D_FF d_ff_3 (.D(Instr_Fetch), .C(clk), .Q(Instr_Decode));  // open: nQ
  D_FF #(.Default(1)) d_ff_4 (.D(Write_Back), .C(clk), .Q(Instr_Fetch));  // open: nQ
endmodule
