// Digital circuit Full-Implementation.dig as structural Verilog
module Full_Implementation (
  input  CLK,
  input  [7:0] InstrMem_input,
  input  [1:0] InstrMem_ctrl,
  output [7:0] IR_output,
  output Instr_Fetch,
  output Instr_Decode,
  output Instr_Exec,
  output Write_Back,
  output [2:0] Program_Counter,
  output IR_ctrl,
  output [7:0] RegFile_ctrl,
  output [7:0] ALU_Output
);

  wire [7:0] full_memory_1_p5, multiplexer_2_out, multiplexer_4_out, register_file_1_read_data1,
       register_file_1_read_data2;
  wire [7:3] _8_bit_pc_1_output;

  _8_Bit_PC _8_bit_pc_1 (
    .CLK(CLK), .CTRL({1'b0, Write_Back}), .INC_by(8'h1), .Output({_8_bit_pc_1_output, Program_Counter}));
  // Full_Memory full_memory_1: pin names not known; wires that end beside it: Program_Counter, CLK, InstrMem_input, InstrMem_ctrl, full_memory_1_p5
  Multiplexer multiplexer_1 (.sel(InstrMem_ctrl[0]), .in_0(Instr_Fetch), .in_1(1'b0), .out(IR_ctrl));
  Instruction_Register instruction_register_1 (
    .CTRL(IR_ctrl), .clk(CLK), .Data_In(full_memory_1_p5), .Output(IR_output));
  Control_Unit control_unit_1 (
    .clk(CLK), .Instr_Fetch(Instr_Fetch), .Instr_Decode(Instr_Decode), .Instr_Exec(Instr_Exec),
    .Write_Back(Write_Back));
  Multiplexer #(.Selector_Bits(2), .Bits(8)) multiplexer_2 (
    .sel(IR_output[4:3]), .in_0(8'h1), .in_1(8'h4), .in_2(8'h10), .in_3(8'h40), .out(multiplexer_2_out));
  Multiplexer #(.Bits(8)) multiplexer_3 (
    .sel(Instr_Decode), .in_0({8{1'b0}}), .in_1(multiplexer_2_out), .out(RegFile_ctrl));
  Register_File register_file_1 (
    .clk(CLK), .Read_Register1(IR_output[4:3]), .Read_Register2(IR_output[2:1]), .Write_Data(ALU_Output),
    .Write_Register(IR_output[4:3]), .ctrl(RegFile_ctrl), .Read_Data1(register_file_1_read_data1),
    .Read_Data2(register_file_1_read_data2));
  Multiplexer #(.Bits(8)) multiplexer_4 (
    .sel(IR_output[0]), .in_0(register_file_1_read_data1), .in_1({{6{1'b0}}, IR_output[2:1]}),
    .out(multiplexer_4_out));
  _8BitALU _8bitalu_1 (
    .A(multiplexer_4_out), .S_1_S_0_Carry_In(IR_output[7:5]), .B(register_file_1_read_data2),
    .Result(ALU_Output));  // open: Status

  // Notes on the sheet:
  //   1. Instruction Fetch
  //   2. Instruction Decode
  //   3. Instruction Execution (Exec)
endmodule

/* Test case:
# =========================================================
# 8-bit processor test
#
# Signals:
#   clk Program_Counter InstrMem_input InstrMem_ctrl
#   IR_output IR_ctrl Write_Back ALU_output
#
# Instruction format:
#   [ opcode(3) | op1(2) | op2(2) | type(1) ]
#
# opcode = ALU control bits = S1 S0 Cin
#
# ALU control / opcode meanings:
#   000 = A + B                  (ADD)
#   001 = A + B + 1              (ADD with carry)
#   010 = A + B̅                 (SUB with borrow)
#   011 = A + B̅ + 1             (SUB)
#   100 = A                      (TRANSFER A)
#   101 = A + 1                  (INCREMENT A)
#   110 = A - 1                  (DECREMENT A)
#   111 = A                      (TRANSFER A)
#
# Register encoding:
#   00 = R0
#   01 = R1
#   10 = R2
#   11 = R3
#
# Type bit:
#   0 = R-type
#   1 = I-type
#
# Notes:
# - In R-type, op1 is A and destination, op2 selects register B.
# - In I-type, op2 is the 2-bit immediate value.
# - TRANSFER A should be encoded as I-type here, with op2 filled
#   as an immediate field.
# - Registers are assumed to start at 0.
#
# Program:
#   0: INC   R1        ; R1 = 1
#   1: INC   R1        ; R1 = 2
#   2: ADDI  R2, 3     ; R2 = 3
#   3: ADD   R2, R1    ; R2 = 5
#   4: SUB   R2, R1    ; R2 = 3
#   5: SUBB  R2, R1    ; R2 = 0
#   6: INC   R0        ; R0 = 1
#   7: DEC   R0        ; R0 = 0
#   8: TRANSFER A R2   ; I-type, imm=01, R2 stays 0
#   9: TRANSFER A R2   ; I-type, imm=10, R2 stays 0
# =========================================================

clk Program_Counter InstrMem_input InstrMem_ctrl IR_output IR_ctrl Write_Back ALU_output

# ---------------------------------------------------------
# settle
# ---------------------------------------------------------
#repeat(10) C X 0 0 X X X X

# ---------------------------------------------------------
# program instruction memory
# ---------------------------------------------------------

# ---------------------------------------------------------
# addr 0 : 168 = INC R1
#
# 168 = 0xA8 = 10101000
#
# Breakdown:
#   opcode = 101  -> Increment A
#   op1    = 01   -> R1
#   op2    = 00   -> immediate field present but ignored by INC
#   type   = 0    -> R-type
#
# Meaning:
#   R1 <- R1 + 1
# ---------------------------------------------------------
C X 168 1 X X X X
repeat(3) C X 0 0 X X X X

# ---------------------------------------------------------
# addr 1 : 168 = INC R1
#
# Same instruction again
# Meaning:
#   R1 <- R1 + 1
# ---------------------------------------------------------
C X 168 1 X X X X
repeat(3) C X 0 0 X X X X

C X 168 1 X X X X
repeat(3) C X 0 0 X X X X

C X 168 1 X X X X
repeat(3) C X 0 0 X X X X

# ---------------------------------------------------------
# addr 0 : 168 = INC R2
#
# 176 = 0xA8 = 10110000
#
# Breakdown:
#   opcode = 101  -> Increment A
#   op1    = 10   -> R2
#   op2    = 00   -> immediate field present but ignored by INC
#   type   = 0    -> R-type
#
# Meaning:
#   R2 <- R2 + 1
# ---------------------------------------------------------
C X 176 1 X X X X
repeat(3) C X 0 0 X X X X


C X 176 1 X X X X
repeat(3) C X 0 0 X X X X



# ---------------------------------------------------------
# addr 4 : 114 = SUB R1, R2
#
# 108 = 0x6C = 011 01 10 0
#
# Breakdown:
#   opcode = 011  -> Subtract
#   op1    = 01   -> R2
#   op2    = 10   -> R1
#   type   = 0    -> R-type
#
# Meaning:
#   R2 <- R2 - R1
# ---------------------------------------------------------
C X 108 1 X X X X
repeat(3) C X 0 0 X X X X



# ---------------------------------------------------------
# stop programming
# ---------------------------------------------------------
repeat(2) C X 0 0 X X X X

# ---------------------------------------------------------
# run
# ---------------------------------------------------------
# Expected high-level behavior:
#   R1: 0 -> 1 -> 2
#   R2: 0 -> 3 -> 5 -> 3 -> 0 -> 0 -> 0
#   R0: 0 -> 1 -> 0
# ---------------------------------------------------------
repeat(40) C X 0 0 X X X X
*/
