// Digital circuit Instruction Register.dig as structural Verilog
module Instruction_Register (
  input  CTRL,
  input  clk,
  input  [7:0] Data_In,
  output [7:0] Output
);

  wire [7:0] _8_bit_1_p4;

  // _8_Bit _8_bit_1: pin names not known; wires that end beside it: clk, 2'b01, Output, _8_bit_1_p4
  Multiplexer #(.Bits(8)) multiplexer_1 (.sel(CTRL), .in_0(_8_bit_1_p4), .in_1(Data_In), .out(Output));

  // Notes on the sheet:
  //   CTRL: LD
endmodule
