// Digital circuit Register File.dig as structural Verilog
module Register_File (
  input  clk,
  input  [1:0] Read_Register1,
  input  [1:0] Read_Register2,
  input  [7:0] Write_Data,
  input  [1:0] Write_Register,
  input  [7:0] ctrl,
  output [7:0] Read_Data1,
  output [7:0] Read_Data2
);

  wire [7:0] demultiplexer_1_out_0, demultiplexer_1_out_1, demultiplexer_1_out_2, demultiplexer_1_out_3,
       R0_p4, R1_p4, R2_p4, R3_p4;

  Demultiplexer #(.Bits(8), .Selector_Bits(2)) demultiplexer_1 (
    .sel(Write_Register), .in(Write_Data), .out_0(demultiplexer_1_out_0), .out_1(demultiplexer_1_out_1),
    .out_2(demultiplexer_1_out_2), .out_3(demultiplexer_1_out_3));
  // _8_Bit R0: pin names not known; wires that end beside it: clk, ctrl[1:0], demultiplexer_1_out_0, R0_p4
  // _8_Bit R1: pin names not known; wires that end beside it: clk, ctrl[3:2], demultiplexer_1_out_1, R1_p4
  // _8_Bit R2: pin names not known; wires that end beside it: clk, ctrl[5:4], demultiplexer_1_out_2, R2_p4
  // _8_Bit R3: pin names not known; wires that end beside it: clk, ctrl[7:6], demultiplexer_1_out_3, R3_p4
  Multiplexer #(.Bits(8), .Selector_Bits(2)) multiplexer_1 (
    .sel(Read_Register1), .in_0(R0_p4), .in_1(R1_p4), .in_2(R2_p4), .in_3(R3_p4), .out(Read_Data1));
  Multiplexer #(.Bits(8), .Selector_Bits(2)) multiplexer_2 (
    .sel(Read_Register2), .in_0(R0_p4), .in_1(R1_p4), .in_2(R2_p4), .in_3(R3_p4), .out(Read_Data2));
endmodule
